// Logisim project Amar3.circ as structural Verilog: 3 circuits, main circuit main
module KMAP_FOR_3 (
  input  A,
  input  B,
  input  C,
  output F
);

  wire and_1_out, not_1_out;

  not not_1 (not_1_out, A);
  and and_1 (and_1_out, not_1_out, B);
  or or_1 (F, C, and_1_out);
endmodule

module KMAP (
  input  A,
  input  B,
  input  C,
  input  A_2,
  input  B_2,
  input  C_2,
  output F,
  output out_8
);

  wire and_1_out, and_2_out, and_3_out, and_4_out, and_5_out, and_6_out, not_1_out, not_2_out, not_3_out,
       not_4_out;

  not not_1 (not_1_out, A);
  and and_1 (and_1_out, not_1_out, B);
  or or_1 (F, C, and_1_out);
  not not_2 (not_2_out, A_2);
  not not_3 (not_3_out, B_2);
  not not_4 (not_4_out, C_2);
  and and_2 (and_2_out, not_2_out, not_3_out, C_2);
  and and_3 (and_3_out, not_2_out, B_2, not_4_out);
  and and_4 (and_4_out, not_2_out, B_2, C_2);
  and and_5 (and_5_out, A_2, not_3_out, C_2);
  and and_6 (and_6_out, A_2, B_2, C_2);
  or or_2 (out_8, and_2_out, and_3_out, and_4_out, and_5_out, and_6_out);
endmodule

module main (
  input  A,
  input  in_2,
  input  B,
  input  in_4,
  input  A_2,
  input  in_6,
  input  in_7,
  input  FULL_SUBSTRACTOR,
  input  in_9,
  input  in_10,
  output A_B,
  output out_12,
  output A_B_2,
  output out_14,
  output A_B_C,
  output out_16,
  output out_17,
  output out_18
);

  wire and_2_out, and_3_out, and_4_out, and_6_out, and_7_out, and_8_out, not_1_out, not_2_out, not_3_out,
       xor_1_out, xor_5_out;

  xor xor_1 (xor_1_out, A_2, in_6);
  xor xor_2 (A_B, A, A);
  and and_1 (A_B_2, A, A);
  and and_2 (and_2_out, in_6, in_6);
  and and_3 (and_3_out, A_2, in_6);
  and and_4 (and_4_out, A_2, in_6);
  xor xor_3 (A_B_C, xor_1_out, in_6);
  or or_1 (out_17, and_2_out, and_3_out, and_4_out);
  not not_1 (not_1_out, in_4);
  xor xor_4 (out_12, in_2, in_4);
  and and_5 (out_14, not_1_out, in_4);
  xor xor_5 (xor_5_out, FULL_SUBSTRACTOR, in_9);
  not not_2 (not_2_out, FULL_SUBSTRACTOR);
  not not_3 (not_3_out, FULL_SUBSTRACTOR);
  xor xor_6 (out_16, xor_5_out, in_10);
  and and_6 (and_6_out, not_2_out, in_10);
  and and_7 (and_7_out, not_3_out, in_9);
  and and_8 (and_8_out, in_9, in_10);
  or or_2 (out_18, and_6_out, and_7_out, and_8_out);

  assign B = A;
  assign in_7 = in_6;

  // Notes on the sheet:
  //   Y=A+B.AB
  //   FULL ADDER
  //   A+B
  //   HALF ADDER
  //   Y=A+B+C , C+AC+AB
  //   HALF SUBSTRACTOR
endmodule
