// Logisim project Amar5.circ as structural Verilog: 2 circuits, main circuit main
module main (
  input  in_1,
  input  [1:0] in_2,
  input  D,
  input  S1,
  input  S0,
  output F0,
  output F1,
  output F2,
  output F3,
  output out_10
);

  wire and_1_out, and_2_out, and_3_out, and_4_out, not_1_out, not_2_out;

  Demultiplexer #(.select(2), .enable("false")) demultiplexer_1 (
    .out0(F0), .out1(F1), .out2(F2), .out3(F3), .in(in_1), .sel(in_2));
  not not_1 (not_1_out, S1);
  not not_2 (not_2_out, S0);
  and and_1 (and_1_out, not_1_out, not_2_out, D);
  and and_2 (and_2_out, not_1_out, S0, D);
  and and_3 (and_3_out, S1, not_2_out, D);
  and and_4 (and_4_out, S1, S0, D);
  or or_1 (out_10, and_1_out, and_2_out, and_3_out, and_4_out);

  // Notes on the sheet:
  //   DE-MUX
  //   CIRCUIT DIAGRAM
endmodule

module MUX (
  input  A,
  input  B,
  input  C,
  output F
);

  wire and_1_out, and_2_out, and_3_out, not_1_out, not_2_out, not_3_out;

  not not_1 (not_1_out, A);
  not not_2 (not_2_out, B);
  not not_3 (not_3_out, C);
  and and_1 (and_1_out, not_1_out, not_2_out, C);
  and and_2 (and_2_out, B, not_3_out);
  and and_3 (and_3_out, A, B);
  or or_1 (F, and_1_out, and_2_out, and_3_out);
endmodule
