// Logisim project Amar6.circ as structural Verilog: 1 circuit, main circuit main
module main (
  input  J,
  input  [3:0] in_2,
  input  K,
  input  [3:0] in_4,
  input  CIRCUIT_DIAGRAM,
  input  D,
  input  in_7,
  input  T,
  output out_9,
  output out_10,
  output out_11,
  output out_12,
  output out_13,
  output out_14,
  output out_15,
  output out_16,
  output out_17,
  output out_18,
  output out_19,
  output out_20
);

  wire clock_1_out, clock_2_out, clock_3_out, not_1_out, not_2_out;

  Comparator #(.width(4)) comparator_1 (.a(in_2), .b(in_4), .gt(out_10), .eq(out_12), .lt(out_13));
  not not_1 (not_1_out, in_7);
  not not_2 (not_2_out, CIRCUIT_DIAGRAM);
  and and_1 (out_15, CIRCUIT_DIAGRAM, not_1_out);
  xnor xnor_1 (out_17, CIRCUIT_DIAGRAM, in_7);
  or or_1 (out_19, not_2_out, in_7);
  Clock clock_1 (.out(clock_1_out));
  Clock clock_2 (.out(clock_2_out));
  Clock clock_3 (.out(clock_3_out));
  J_K_Flip_Flop j_k_ff_1 (.J(J), .clk(clock_1_out), .K(K), .Q(out_9), .Qn(out_11));  // open: preset, en, reset
  D_Flip_Flop d_ff_1 (.clk(clock_2_out), .D(D), .Q(out_14), .Qn(out_16));  // open: preset, en, reset
  T_Flip_Flop t_ff_1 (.clk(clock_3_out), .T(T), .Q(out_18), .Qn(out_20));  // open: preset, reset, en

  // Notes on the sheet:
  //   ONE BIT 
  //   MAGNITUDE 
  //   COMPARAOTOR
  //   P15
  //   CLOCK
  //   J K FLIP FLOP
  //   CLOCK
  //   CLOCK
  //   D FLIP FLOP
  //   T FLIP FLOP
endmodule
